# Fritzing sketch working diagram (saved by Fritzing 0.9.3b)

parts:
  U1 = ESP8266 WiFi Module [part_number=ESP8266]
  IC1 = Voltage Regulator AMS1117 [package=sot223]
  U2 = 2-Channel 5v Relay Shield [package=relay-2ch5v10a]

nets:
  VCC: U1.VCC, U1.CH_PD, IC1.OUT, U2.VCC
  N1: U1.GPIO_0, U2.IN1
  N2: U1.GPIO_2, U2.IN2
  GND: U1.GND, IC1.GND

custom parts:
  ESP8266 WiFi Module: Generic WiFi Module based on the ESP8266 with onboard PCB antenna and UART communications
  2-Channel 5v Relay Shield: 2 Channel 5v Relay Shield w. 2x SPD-06VDC-SD-C
